# Fritzing sketch final_circuit (saved by Fritzing 0.9.3b)
breadboards: 4

parts:
  S1 = Pushbutton [package="[THT]"]
  S2 = Pushbutton [package="[THT]"]
  S3 = Pushbutton [package="[THT]"]
  S4 = Pushbutton [package="[THT]"]
  S5 = Pushbutton [package="[THT]"]
  S6 = Pushbutton [package="[THT]"]
  S7 = Pushbutton [package="[THT]"]
  S8 = Pushbutton [package="[THT]"]
  S9 = Pushbutton [package="[THT]"]
  IC2 = SHIFT REGISTER [package=dil16]
  IC3 = SHIFT REGISTER [package=dil16]
  IC4 = SHIFT REGISTER [package=dil16]
  Part3 = Arduino Uno (Rev3)
  LED1 = RGB LED - (4 legs) [package="5 mm [THT]"]
  LED2 = RGB LED - (4 legs) [package="5 mm [THT]"]
  LED3 = RGB LED - (4 legs) [package="5 mm [THT]"]
  LED4 = RGB LED - (4 legs) [package="5 mm [THT]"]
  LED5 = RGB LED - (4 legs) [package="5 mm [THT]"]
  LED6 = RGB LED - (4 legs) [package="5 mm [THT]"]
  LED7 = RGB LED - (4 legs) [package="5 mm [THT]"]
  LED8 = RGB LED - (4 legs) [package="5 mm [THT]"]
  LED9 = RGB LED - (4 legs) [package="5 mm [THT]"]
  R1 = Resistor [tolerance=±5% resistance=220 package="2010 [SMD]"]
  R2 = Resistor [tolerance=±5% resistance=220 package="2010 [SMD]"]
  R3 = Resistor [tolerance=±5% resistance=220 package="2010 [SMD]"]
  R4 = Resistor [tolerance=±5% resistance=220 package="2010 [SMD]"]
  R5 = Resistor [tolerance=±5% resistance=220 package="2010 [SMD]"]
  R6 = Resistor [tolerance=±5% resistance=220 package="2010 [SMD]"]
  R7 = Resistor [tolerance=±5% resistance=220 package="2010 [SMD]"]
  R8 = Resistor [tolerance=±5% resistance=220 package="2010 [SMD]"]
  R9 = Resistor [tolerance=±5% resistance=220 package="2010 [SMD]"]
  R10 = Resistor [tolerance=±5% resistance=220 package="2010 [SMD]"]
  R11 = Resistor [tolerance=±5% resistance=220 package="2010 [SMD]"]
  R12 = Resistor [tolerance=±5% resistance=220 package="2010 [SMD]"]
  R13 = Resistor [tolerance=±5% resistance=220 package="2010 [SMD]"]
  R14 = Resistor [tolerance=±5% resistance=220 package="2010 [SMD]"]
  R15 = Resistor [tolerance=±5% resistance=220 package="2010 [SMD]"]
  R16 = Resistor [tolerance=±5% resistance=220 package="2010 [SMD]"]
  R17 = Resistor [tolerance=±5% resistance=220 package="2010 [SMD]"]
  R18 = Resistor [tolerance=±5% resistance=220 package="2010 [SMD]"]

nets:
  N1: S1.Pin_1, S1.Pin_2, Part3.D5_PWM
  GND: S1.Pin_3, S1.Pin_4, S2.Pin_3, S2.Pin_4, S3.Pin_3, S3.Pin_4, S4.Pin_3, S4.Pin_4, S5.Pin_3, S5.Pin_4, S6.Pin_3, S6.Pin_4, S7.Pin_3, S7.Pin_4, S8.Pin_3, S8.Pin_4, S9.Pin_3, S9.Pin_4, IC2.GND, IC2.G, IC3.GND, IC3.G, IC4.GND, IC4.G, Part3.GND
  N2: S2.Pin_1, S2.Pin_2, Part3.D9_PWM
  N3: S3.Pin_1, S3.Pin_2, Part3.D2
  N4: S4.Pin_1, S4.Pin_2, Part3.D10_PWM/SS
  N5: S5.Pin_1, S5.Pin_2, Part3.D6_PWM
  N6: S6.Pin_1, S6.Pin_2, Part3.D3_PWM
  N7: S7.Pin_1, S7.Pin_2, Part3.D4
  N8: S8.Pin_1, S8.Pin_2, Part3.D7
  N9: S9.Pin_1, S9.Pin_2, Part3.D13/SCK
  N10: IC2.QB, R2.Pin_0
  N11: IC2.QC, R7.Pin_0
  N12: IC2.QD, R8.Pin_0
  N13: IC2.QE, R13.Pin_0
  N14: IC2.QF, R14.Pin_0
  N15: IC2.QH*, IC3.SER
  VCC: IC2.SCL, IC2.VCC, IC3.SCL, IC3.VCC, IC4.SCL, IC4.VCC, Part3.5V, LED1.green_cathode, LED2.green_cathode, LED3.green_cathode, LED4.green_cathode, LED5.green_cathode, LED6.green_cathode, LED7.green_cathode, LED8.green_cathode, LED9.green_cathode
  N16: IC2.SCK, IC3.SCK, IC4.SCK, Part3.D12/MISO
  N17: IC2.RCK, IC3.RCK, IC4.RCK, Part3.D8
  N18: IC2.SER, Part3.D11_PWM/MOSI
  N19: IC2.QA, R1.Pin_0
  N20: IC3.QB, R4.Pin_0
  N21: IC3.QC, R9.Pin_0
  N22: IC3.QD, R10.Pin_0
  N23: IC3.QE, R15.Pin_0
  N24: IC3.QF, R16.Pin_0
  N25: IC3.QH*, IC4.SER
  N26: IC3.QA, R3.Pin_0
  N27: IC4.QB, R6.Pin_0
  N28: IC4.QC, R11.Pin_0
  N29: IC4.QD, R12.Pin_0
  N30: IC4.QE, R17.Pin_0
  N31: IC4.QF, R18.Pin_0
  N32: IC4.QA, R5.Pin_0
  N33: LED1.red_cathode, R2.Pin_1
  N34: LED1.common_anode, R1.Pin_1
  N35: LED2.red_cathode, R4.Pin_1
  N36: LED2.common_anode, R3.Pin_1
  N37: LED3.red_cathode, R6.Pin_1
  N38: LED3.common_anode, R5.Pin_1
  N39: LED4.red_cathode, R8.Pin_1
  N40: LED4.common_anode, R7.Pin_1
  N41: LED5.red_cathode, R12.Pin_1
  N42: LED5.common_anode, R11.Pin_1
  N43: LED6.red_cathode, R10.Pin_1
  N44: LED6.common_anode, R9.Pin_1
  N45: LED7.red_cathode, R14.Pin_1
  N46: LED7.common_anode, R13.Pin_1
  N47: LED8.red_cathode, R16.Pin_1
  N48: LED8.common_anode, R15.Pin_1
  N49: LED9.red_cathode, R18.Pin_1
  N50: LED9.common_anode, R17.Pin_1
